// Logisim project 4CalculationWithController.circ as structural Verilog: 1 circuit, main circuit main
module main (
  input  [3:0] Operand_A,
  input  [1:0] in_2,
  input  [3:0] Operand_B
);

  wire [3:0] adder_1_out, divider_1_out, multiplexer_1_out, multiplier_1_out, subtractor_1_out;

  Adder #(.width(4)) adder_1 (.a(Operand_A), .b(Operand_B), .out(adder_1_out));  // open: cin, cout
  Subtractor #(.width(4)) subtractor_1 (.a(Operand_A), .b(Operand_B), .out(subtractor_1_out));  // open: bin, bout
  Multiplier #(.width(4)) multiplier_1 (.a(Operand_A), .b(Operand_B), .out(multiplier_1_out));  // open: cin, cout
  Divider #(.width(4)) divider_1 (.a(Operand_A), .b(Operand_B), .out(divider_1_out));  // open: upper, rem
  Multiplexer #(.select(2), .width(4)) multiplexer_1 (
    .in0(adder_1_out), .in1(subtractor_1_out), .in2(multiplier_1_out), .in3(divider_1_out),
    .out(multiplexer_1_out), .sel(in_2));
  // Probe on multiplexer_1_out
  // Probe on multiplexer_1_out

  // Notes on the sheet:
  //   4-Bit Adder
  //   4-Bit Subtractor
  //   4-Bit Multiplier
  //   4-Bit Divider
  //   Bus Controller / MUX
  //   OP Select (00-11)
  //   Binary Output
  //   Decimal Result
endmodule
